# Fritzing sketch swachha bharat (saved by Fritzing 0.9.3b)
breadboards: 1

parts:
  R1 = Resistor [tolerance=±5% resistance=2k package=THT]
  R2 = Resistor [tolerance=±5% resistance=1k package=THT]
  R3 = Resistor [tolerance=±5% resistance=2k package=THT]
  R4 = Resistor [tolerance=±5% resistance=2k package=THT]
  R5 = Resistor [tolerance=±5% resistance=2k package=THT]
  R6 = Resistor [tolerance=±5% resistance=1k package=THT]
  R7 = Resistor [tolerance=±5% resistance=1k package=THT]
  R8 = Resistor [tolerance=±5% resistance=1k package=THT]
  Raspberry_Pi_1 = Raspberry Pi 3 [part_number=RPI-3-V1.2]
  hc-sr1 = hc-sr04
  Part1 = Soil Moisture Sensor
  hc-sr2 = hc-sr04
  Part2 = Soil Moisture Sensor
  LCD1 = LCD screen

nets (from the breadboard view):
  N1: R1.Pin_0, R2.Pin_1, Raspberry_Pi_1.GPIO3
  GND: R1.Pin_1, R3.Pin_1, R4.Pin_1, R5.Pin_1, Raspberry_Pi_1.GND, hc-sr1.GND, Part1.GND, hc-sr2.GND, Part2.GND, LCD1.R/W, LCD1.DB7
  N2: R2.Pin_0, hc-sr2.Echo
  N3: R3.Pin_0, R7.Pin_1, Raspberry_Pi_1.GPIO27
  N4: R4.Pin_0, R8.Pin_1, Raspberry_Pi_1.GPIO2
  N5: R5.Pin_0, R6.Pin_1, Raspberry_Pi_1.GPIO22
  N6: R6.Pin_0, Part2.SIG
  N7: R7.Pin_0, hc-sr1.Echo
  N8: R8.Pin_0, Part1.SIG
  N9: Raspberry_Pi_1.GPIO4, hc-sr2.Trig
  N10: Raspberry_Pi_1.GPIO17, hc-sr1.Trig
  N11: Raspberry_Pi_1.GPIO12, LCD1.RS
  N12: Raspberry_Pi_1.ID_SC, LCD1.E
  N13: Raspberry_Pi_1.GPIO7, LCD1.DB4
  N14: Raspberry_Pi_1.GPIO8, LCD1.DB5
  N15: Raspberry_Pi_1.GPIO25, LCD1.DB6
  VCC: Raspberry_Pi_1.5V, hc-sr1.VCC, Part1.VCC, hc-sr2.VCC, Part2.VCC
