# Fritzing sketch rpi lcd (saved by Fritzing 0.9.3b)
breadboards: 1

parts:
  Raspberry_Pi_1 = Raspberry Pi 3 [part_number=RPI-3-V1.2]
  LCD1 = LCD screen
  U1 = POT [package=trim_pot]

nets:
  GND: Raspberry_Pi_1.GND, LCD1.VSS, LCD1.R/W, LCD1.LED-, U1.E
  N1: Raspberry_Pi_1.GIPO7, LCD1.RS
  N2: Raspberry_Pi_1.GIPO8, LCD1.E
  N3: Raspberry_Pi_1.GIPO25, LCD1.DB4
  N4: Raspberry_Pi_1.GIPO24, LCD1.DB5
  N5: Raspberry_Pi_1.GIPO23, LCD1.DB6
  N6: Raspberry_Pi_1.GIPO18, LCD1.DB7
  5V: Raspberry_Pi_1.5V, LCD1.VDD, LCD1.LED+, U1.A
  N7: LCD1.V0, U1.S
